// Logisim project 4BITADDER.circ as structural Verilog: 1 circuit, main circuit main
module main (
  input  [3:0] A,
  input  [3:0] B,
  output [3:0] Sum,
  output overflow
);

  wire main_1_carry, main_2_carry, main_3_carry;

  fulladder_main main_1 (.carry_in(1'b0), .A_in(A[0]), .B_in(B[0]), .sum(Sum[0]), .carry(main_1_carry));
  fulladder_main main_2 (.carry_in(main_1_carry), .A_in(A[1]), .B_in(B[1]), .sum(Sum[1]), .carry(main_2_carry));
  fulladder_main main_3 (.carry_in(main_2_carry), .A_in(A[2]), .B_in(B[2]), .sum(Sum[2]), .carry(main_3_carry));
  fulladder_main main_4 (.carry_in(main_3_carry), .A_in(A[3]), .B_in(B[3]), .sum(Sum[3]), .carry(overflow));
endmodule
