// Logisim project 4bitadder.circ as structural Verilog: 1 circuit, main circuit main
module main (
  input  in_1,
  input  in_2,
  input  in_3,
  input  in_4,
  input  in_5,
  input  in_6,
  input  in_7,
  input  in_8,
  input  in_9,
  output out_10,
  output out_11,
  output out_12,
  output out_13,
  output out_14
);

  wire main_2_carry, main_3_carry, main_4_carry;

  fulladder_main main_1 (.carry_in(main_2_carry), .A_in(in_6), .B_in(in_5), .sum(out_12), .carry(out_10));
  fulladder_main main_2 (.carry_in(main_3_carry), .A_in(in_2), .B_in(in_1), .sum(out_13), .carry(main_2_carry));
  fulladder_main main_3 (.carry_in(main_4_carry), .A_in(in_4), .B_in(in_3), .sum(out_14), .carry(main_3_carry));
  fulladder_main main_4 (.carry_in(in_9), .A_in(in_8), .B_in(in_7), .sum(out_11), .carry(main_4_carry));
endmodule
