// Logisim project fulladder.circ as structural Verilog: 1 circuit, main circuit main
// fell adder
module main (
  input  carry_in,
  input  A_in,
  input  B_in,
  output sum,
  output carry
);

  wire main_1_carry, main_1_sum_1, main_2_carry;

  halfadder_main main_1 (.A_in(A_in), .B_in(B_in), .sum_1(main_1_sum_1), .carry(main_1_carry));
  halfadder_main main_2 (.A_in(carry_in), .B_in(main_1_sum_1), .sum_1(sum), .carry(main_2_carry));
  or or_1 (carry, main_2_carry, main_1_carry);
endmodule
