// Logisim project halfadder.circ as structural Verilog: 1 circuit, main circuit main
// Half adder
module main (
  input  A_in,
  input  B_in,
  output sum_1,
  output carry
);

  xor xor_1 (sum_1, A_in, B_in);
  and and_1 (carry, A_in, B_in);
endmodule
