// Logisim project thereal4bit.circ as structural Verilog: 2 circuits, main circuit full adder
module full_adder (
);

  // fulladder_main main_1: pin names not known
endmodule

module ripple_adder (
  input  [3:0] A,
  input  [3:0] B,
  output [3:0] sum,
  output overflow
);

  wire main_1_carry, main_2_carry, main_3_carry;

  fulladder_main main_1 (.carry_in(1'b0), .A_in(A[0]), .B_in(B[0]), .sum(sum[0]), .carry(main_1_carry));
  fulladder_main main_2 (.carry_in(main_1_carry), .A_in(A[1]), .B_in(B[1]), .sum(sum[1]), .carry(main_2_carry));
  fulladder_main main_3 (.carry_in(main_2_carry), .A_in(A[2]), .B_in(B[2]), .sum(sum[2]), .carry(main_3_carry));
  fulladder_main main_4 (.carry_in(main_3_carry), .A_in(A[3]), .B_in(B[3]), .sum(sum[3]), .carry(overflow));
endmodule
