// Logisim project thereal8bit.circ as structural Verilog: 1 circuit, main circuit main
module main (
  input  [7:0] A_in,
  input  [7:0] B_in,
  output [7:0] Sum,
  output C_out
);

  wire main_1_carry, main_2_carry, main_3_carry, main_4_carry, main_5_carry, main_6_carry, main_7_carry;

  fulladder_main main_1 (.carry_in(1'b0), .A_in(A_in[0]), .B_in(B_in[0]), .sum(Sum[0]), .carry(main_1_carry));
  fulladder_main main_2 (.carry_in(main_1_carry), .A_in(A_in[1]), .B_in(B_in[1]), .sum(Sum[1]), .carry(main_2_carry));
  fulladder_main main_3 (.carry_in(main_2_carry), .A_in(A_in[2]), .B_in(B_in[2]), .sum(Sum[2]), .carry(main_3_carry));
  fulladder_main main_4 (.carry_in(main_3_carry), .A_in(A_in[3]), .B_in(B_in[3]), .sum(Sum[3]), .carry(main_4_carry));
  fulladder_main main_5 (.carry_in(main_4_carry), .A_in(A_in[4]), .B_in(B_in[4]), .sum(Sum[4]), .carry(main_5_carry));
  fulladder_main main_6 (.carry_in(main_5_carry), .A_in(A_in[5]), .B_in(B_in[5]), .sum(Sum[5]), .carry(main_6_carry));
  fulladder_main main_7 (.carry_in(main_6_carry), .A_in(A_in[6]), .B_in(B_in[6]), .sum(Sum[6]), .carry(main_7_carry));
  fulladder_main main_8 (.carry_in(main_7_carry), .A_in(A_in[7]), .B_in(B_in[7]), .sum(Sum[7]), .carry(C_out));

  // Notes on the sheet:
  //   Jwinberry
endmodule
